# Fritzing sketch ESP para-site - ESP12F Advanced (saved by Fritzing 0.9.3b)

parts:
  NodeMCU1 = NodeMCU V1.0
  J19 = female pin header, 5 pins [form="♀ (female)"]
  J20 = double row female pin header, 4 pins [form="♀ (female)"]
  CBD_Wifi_Header1 = double row female pin header, 4 pins [form="♀ (female)"]
  J21 = female pin header, 1 pin [form="♀ (female)"]
  S2 = Pushbutton [package="[THT]"]
  2_Channel_Relay1 = 2 Channel Power Relay
  J22 = screw terminal, 2 pins
  +5VDC = screw terminal, 2 pins
  GND1 = screw terminal, 2 pins
  GND1_2 = screw terminal, 2 pins

nets:
  N1: NodeMCU1.D1, J19.pin1, J20.pin2
  N2: NodeMCU1.D2, J19.pin2, J20.pin3
  N3: NodeMCU1.GND, NodeMCU1.D7, J19.pin4, J20.pin4, S2.Pin_1, S2.Pin_2
  N4: NodeMCU1.D5, 2_Channel_Relay1.IN1
  N5: NodeMCU1.D6, 2_Channel_Relay1.IN2
  3V3: NodeMCU1.3V3, J19.pin3, CBD_Wifi_Header1.pin1, 2_Channel_Relay1.VCC
  N6: J19.pin5, J21.pin1, GND1.pin1, GND1_2.pin1
  N7: 2_Channel_Relay1.JD-VCC, J22.pin2, +5VDC.pin2
  N8: 2_Channel_Relay1.GND, J22.pin1, +5VDC.pin1

notes:
  To Sensors

custom parts:
  NodeMCU V1.0: ESP8266 based NodeMCU
  2 Channel Power Relay: A 2 channel power relay. The module operates at 5V.
